// Logisim project SimpleVGACard-TTL.circ as structural Verilog: 1 circuit, main circuit main
module main (
);

  wire clock_1_out, n27c512_1__11__o0, n27c512_1__12__o1, n27c512_1__13__o2, n27c512_1__15__o3,
       n27c512_1__16__o4, n27c512_1__17__o5, n27c512_1__18__o6, n27c512_1__19__o7, n7400_1__3__1y,
       n7400_1__6__2y, n7400_1__8__3y, n7400_1__11__4y, n7400_2__3__1y, n7400_2__6__2y, n7400_2__8__3y,
       n7400_2__11__4y, n7400_3__8__3y, n7404_1__2__1y, n7404_1__4__2y, n7404_1__6__3y, n7404_1__8__4y,
       n7404_2__2__1y, n7404_2__4__2y, n7404_2__6__3y, n7404_2__8__4y, n7404_2__10__5y, n7404_3__2__1y,
       n7404_3__4__2y, n7404_3__6__3y, n7404_3__8__4y, n7404_4__2__1y, n7404_4__4__2y, n7404_4__6__3y,
       n7404_4__8__4y, n7404_4__10__5y, n7404_4__12__6y, n7430_1__8__3y, n7430_2__8__3y, n7430_3__8__3y,
       n7430_4__8__3y, n7430_5__8__3y, n7430_6__8__3y, n7430_7__8__3y, n7430_8__8__3y, n74161_1__15__tc,
       n74161_2__15__tc, n74161_4__15__tc, n74161_5__15__tc;
  wire [0:0] n74161_3__14__q0;
  wire [1:0] n74161_6__14__q0;
  wire [3:0] n74161_1__14__q0, n74161_2__14__q0, n74161_4__14__q0, n74161_5__14__q0;

  Clock clock_1 (.out(clock_1_out));
  _74161 u_74161_1 (
    ._1__nMR(n7430_7__8__3y), ._2__CP(clock_1_out), ._7__CEP(1'b1), ._15__TC(n74161_1__15__tc),
    ._14__Q0(n74161_1__14__q0[0]), ._13__Q1(n74161_1__14__q0[1]), ._12__Q2(n74161_1__14__q0[2]),
    ._11__O3(n74161_1__14__q0[3]), ._10__CET(1'b1), ._9__nPE(1'b1));  // open: _3__D0, _4__D1, _5__D2, _6__D3, _8__GND, _16__Vcc
  _74161 u_74161_2 (
    ._1__nMR(n7430_7__8__3y), ._2__CP(clock_1_out), ._7__CEP(1'b1), ._15__TC(n74161_2__15__tc),
    ._14__Q0(n74161_2__14__q0[0]), ._13__Q1(n74161_2__14__q0[1]), ._12__Q2(n74161_2__14__q0[2]),
    ._11__O3(n74161_2__14__q0[3]), ._10__CET(n74161_1__15__tc), ._9__nPE(1'b1));  // open: _3__D0, _4__D1, _5__D2, _6__D3, _8__GND, _16__Vcc
  _74161 u_74161_3 (
    ._1__nMR(n7430_7__8__3y), ._2__CP(clock_1_out), ._7__CEP(1'b1), ._14__Q0(n74161_3__14__q0[0]),
    ._10__CET(n74161_2__15__tc), ._9__nPE(1'b1));  // open: _3__D0, _4__D1, _5__D2, _6__D3, _8__GND, _16__Vcc, _15__TC, _13__Q1, _12__Q2, _11__O3
  _74161 u_74161_4 (
    ._1__nMR(n7430_8__8__3y), ._2__CP(n7430_7__8__3y), ._7__CEP(1'b1), ._15__TC(n74161_4__15__tc),
    ._14__Q0(n74161_4__14__q0[0]), ._13__Q1(n74161_4__14__q0[1]), ._12__Q2(n74161_4__14__q0[2]),
    ._11__O3(n74161_4__14__q0[3]), ._10__CET(1'b1), ._9__nPE(1'b1));  // open: _3__D0, _4__D1, _5__D2, _6__D3, _8__GND, _16__Vcc
  _74161 u_74161_5 (
    ._1__nMR(n7430_8__8__3y), ._2__CP(n7430_7__8__3y), ._7__CEP(1'b1), ._15__TC(n74161_5__15__tc),
    ._14__Q0(n74161_5__14__q0[0]), ._13__Q1(n74161_5__14__q0[1]), ._12__Q2(n74161_5__14__q0[2]),
    ._11__O3(n74161_5__14__q0[3]), ._10__CET(n74161_4__15__tc), ._9__nPE(1'b1));  // open: _3__D0, _4__D1, _5__D2, _6__D3, _8__GND, _16__Vcc
  _74161 u_74161_6 (
    ._1__nMR(n7430_8__8__3y), ._2__CP(n7430_7__8__3y), ._7__CEP(1'b1), ._14__Q0(n74161_6__14__q0[0]),
    ._13__Q1(n74161_6__14__q0[1]), ._10__CET(n74161_5__15__tc), ._9__nPE(1'b1));  // open: _3__D0, _4__D1, _5__D2, _6__D3, _8__GND, _16__Vcc, _15__TC, _12__Q2, _11__O3
  _7404 u_7404_1 (
    ._1__1A(n74161_1__14__q0[0]), ._2__1Y(n7404_1__2__1y), ._3__2A(n74161_1__14__q0[1]),
    ._4__2Y(n7404_1__4__2y), ._5__3A(n74161_1__14__q0[2]), ._6__3Y(n7404_1__6__3y),
    ._9__4A(n74161_1__14__q0[3]), ._8__4Y(n7404_1__8__4y));  // open: _7__GND, _14__Vcc, _13__6A, _12__6Y, _11__5A, _10__5Y
  _7404 u_7404_2 (
    ._1__1A(n74161_2__14__q0[0]), ._2__1Y(n7404_2__2__1y), ._3__2A(n74161_2__14__q0[1]),
    ._4__2Y(n7404_2__4__2y), ._5__3A(n74161_2__14__q0[2]), ._6__3Y(n7404_2__6__3y),
    ._11__5A(n74161_3__14__q0[0]), ._10__5Y(n7404_2__10__5y), ._9__4A(n74161_2__14__q0[3]),
    ._8__4Y(n7404_2__8__4y));  // open: _7__GND, _14__Vcc, _13__6A, _12__6Y
  _7404 u_7404_3 (
    ._1__1A(n74161_4__14__q0[0]), ._2__1Y(n7404_3__2__1y), ._3__2A(n74161_4__14__q0[1]),
    ._4__2Y(n7404_3__4__2y), ._5__3A(n74161_4__14__q0[2]), ._6__3Y(n7404_3__6__3y),
    ._9__4A(n74161_4__14__q0[3]), ._8__4Y(n7404_3__8__4y));  // open: _7__GND, _14__Vcc, _13__6A, _12__6Y, _11__5A, _10__5Y
  _7404 u_7404_4 (
    ._1__1A(n74161_5__14__q0[0]), ._2__1Y(n7404_4__2__1y), ._3__2A(n74161_5__14__q0[1]),
    ._4__2Y(n7404_4__4__2y), ._5__3A(n74161_5__14__q0[2]), ._6__3Y(n7404_4__6__3y),
    ._13__6A(n74161_6__14__q0[1]), ._12__6Y(n7404_4__12__6y), ._11__5A(n74161_6__14__q0[0]),
    ._10__5Y(n7404_4__10__5y), ._9__4A(n74161_5__14__q0[3]), ._8__4Y(n7404_4__8__4y));  // open: _7__GND, _14__Vcc
  Hex_Digit_Display hex_digit_display_1 (.value({3'b000, n74161_3__14__q0[0]}));  // open: dp
  Hex_Digit_Display hex_digit_display_2 (.value({2'b00, n74161_6__14__q0}));  // open: dp
  Hex_Digit_Display hex_digit_display_3 (.value(n74161_1__14__q0));  // open: dp
  Hex_Digit_Display hex_digit_display_4 (.value(n74161_2__14__q0));  // open: dp
  Hex_Digit_Display hex_digit_display_5 (.value(n74161_4__14__q0));  // open: dp
  Hex_Digit_Display hex_digit_display_6 (.value(n74161_5__14__q0));  // open: dp
  _7430 u_7430_1 (
    ._1__1A(n7404_1__2__1y), ._2__1B(n7404_1__4__2y), ._3__1C(n7404_1__6__3y), ._4__1D(n74161_1__14__q0[3]),
    ._5__1E(n7404_2__2__1y), ._6__1F(n7404_2__4__2y), ._12__1H(n74161_2__14__q0[2]),
    ._11__1G(n74161_2__14__q0[3]), ._8__3Y(n7430_1__8__3y));  // open: _7__GND, _14__Vcc, _13__NC, _10__NC, _9__NC
  _7430 u_7430_2 (
    ._1__1A(n7404_3__2__1y), ._2__1B(n7404_3__4__2y), ._3__1C(n7404_3__6__3y), ._4__1D(n74161_4__14__q0[3]),
    ._5__1E(n74161_5__14__q0[0]), ._6__1F(n7404_4__4__2y), ._12__1H(n74161_5__14__q0[2]),
    ._11__1G(n74161_6__14__q0[1]), ._8__3Y(n7430_2__8__3y));  // open: _7__GND, _14__Vcc, _13__NC, _10__NC, _9__NC
  _7430 u_7430_3 (
    ._1__1A(n7404_1__2__1y), ._2__1B(n74161_1__14__q0[1]), ._3__1C(n7404_1__6__3y), ._4__1D(n7404_1__8__4y),
    ._5__1E(n74161_2__14__q0[0]), ._6__1F(n7404_2__4__2y), ._12__1H(n74161_2__14__q0[2]),
    ._11__1G(n74161_2__14__q0[3]), ._8__3Y(n7430_3__8__3y));  // open: _7__GND, _14__Vcc, _13__NC, _10__NC, _9__NC
  _7430 u_7430_4 (
    ._1__1A(n74161_4__14__q0[0]), ._2__1B(n7404_3__4__2y), ._3__1C(n7404_3__6__3y),
    ._4__1D(n74161_4__14__q0[3]), ._5__1E(n74161_5__14__q0[0]), ._6__1F(n7404_4__4__2y),
    ._12__1H(n74161_5__14__q0[2]), ._11__1G(n74161_6__14__q0[1]), ._8__3Y(n7430_4__8__3y));  // open: _7__GND, _14__Vcc, _13__NC, _10__NC, _9__NC
  _7430 u_7430_5 (
    ._1__1A(n7404_1__2__1y), ._2__1B(n74161_1__14__q0[1]), ._3__1C(n7404_1__6__3y), ._4__1D(n7404_1__8__4y),
    ._5__1E(n74161_2__14__q0[0]), ._6__1F(n74161_2__14__q0[1]), ._12__1H(n74161_2__14__q0[2]),
    ._11__1G(n74161_2__14__q0[3]), ._8__3Y(n7430_5__8__3y));  // open: _7__GND, _14__Vcc, _13__NC, _10__NC, _9__NC
  _7430 u_7430_6 (
    ._1__1A(n74161_4__14__q0[0]), ._2__1B(n7404_3__4__2y), ._3__1C(n74161_4__14__q0[2]),
    ._4__1D(n74161_4__14__q0[3]), ._5__1E(n74161_5__14__q0[0]), ._6__1F(n7404_4__4__2y),
    ._12__1H(n74161_5__14__q0[2]), ._11__1G(n74161_6__14__q0[1]), ._8__3Y(n7430_6__8__3y));  // open: _7__GND, _14__Vcc, _13__NC, _10__NC, _9__NC
  _7430 u_7430_7 (
    ._1__1A(n7404_1__4__2y), ._2__1B(n7404_1__6__3y), ._3__1C(n74161_1__14__q0[3]), ._4__1D(n7404_2__2__1y),
    ._5__1E(n7404_2__4__2y), ._6__1F(n7404_2__6__3y), ._12__1H(n7404_2__8__4y),
    ._11__1G(n74161_3__14__q0[0]), ._8__3Y(n7430_7__8__3y));  // open: _7__GND, _14__Vcc, _13__NC, _10__NC, _9__NC
  _7430 u_7430_8 (
    ._1__1A(n7404_3__2__1y), ._2__1B(n7404_3__4__2y), ._3__1C(n74161_4__14__q0[2]), ._4__1D(n7404_3__8__4y),
    ._5__1E(n74161_5__14__q0[0]), ._6__1F(n74161_5__14__q0[1]), ._12__1H(n74161_5__14__q0[2]),
    ._11__1G(n74161_6__14__q0[1]), ._8__3Y(n7430_8__8__3y));  // open: _7__GND, _14__Vcc, _13__NC, _10__NC, _9__NC
  _7400 u_7400_1 (
    ._1__1A(n7430_3__8__3y), ._2__1B(n7400_1__6__2y), ._3__1Y(n7400_1__3__1y), ._4__2A(n7400_1__3__1y),
    ._5__2B(n7430_5__8__3y), ._6__2Y(n7400_1__6__2y), ._13__4B(n7430_1__8__3y), ._12__4A(n7400_1__8__3y),
    ._11__4Y(n7400_1__11__4y), ._10__3B(n7400_1__11__4y), ._9__3A(n7430_7__8__3y), ._8__3Y(n7400_1__8__3y));  // open: _7__GND, _14__Vcc
  _7400 u_7400_2 (
    ._1__1A(n7430_4__8__3y), ._2__1B(n7400_2__6__2y), ._3__1Y(n7400_2__3__1y), ._4__2A(n7400_2__3__1y),
    ._5__2B(n7430_6__8__3y), ._6__2Y(n7400_2__6__2y), ._13__4B(n7430_2__8__3y), ._12__4A(n7400_2__8__3y),
    ._11__4Y(n7400_2__11__4y), ._10__3B(n7400_2__11__4y), ._9__3A(n7430_8__8__3y), ._8__3Y(n7400_2__8__3y));  // open: _7__GND, _14__Vcc
  _7400 u_7400_3 (
    ._10__3B(n7400_2__8__3y), ._9__3A(n7400_1__8__3y), ._8__3Y(n7400_3__8__3y));  // open: _1__1A, _2__1B, _3__1Y, _4__2A, _5__2B, _6__2Y, _7__GND, _14__Vcc, _13__4B, _12__4A, _11__4Y
  _27C512 u_27c512_1 (
    ._1__A15(1'b0), ._2__A12(n74161_6__14__q0[0]), ._3__A7(n74161_4__14__q0[3]),
    ._4__A6(n74161_2__14__q0[3]), ._5__A5(n74161_2__14__q0[2]), ._6__A4(n74161_2__14__q0[1]),
    ._7__A3(n74161_2__14__q0[0]), ._8__A2(n74161_1__14__q0[3]), ._9__A1(n74161_1__14__q0[2]),
    ._10__A0(n74161_1__14__q0[1]), ._11__O0(n27c512_1__11__o0), ._12__O1(n27c512_1__12__o1),
    ._13__O2(n27c512_1__13__o2), ._27__A14(1'b0), ._26__A13(n74161_6__14__q0[1]),
    ._25__A8(n74161_5__14__q0[0]), ._24__A9(n74161_5__14__q0[1]), ._23__A11(n74161_5__14__q0[3]),
    ._22__nOE_Vpp(n7400_3__8__3y), ._21__A10(n74161_5__14__q0[2]), ._20__nCE(1'b0),
    ._19__O7(n27c512_1__19__o7), ._18__O6(n27c512_1__18__o6), ._17__O5(n27c512_1__17__o5),
    ._16__O4(n27c512_1__16__o4), ._15__O3(n27c512_1__15__o3));  // open: _14__GND, _28__Vcc
  LED led_1 (.in(n7400_1__3__1y));
  LED led_2 (.in(n7400_2__3__1y));
  LED Red_Signal (.in(n27c512_1__16__o4));
  LED Green_Signal (.in(n27c512_1__13__o2));
  LED Blue_Signal (.in(n27c512_1__11__o0));

  // Notes on the sheet:
  //   10 MHz Clock
  //   Reset
  //   Reset
  //   Pixel Number
  //   (Hexadecimal)
  //   End Line Detector
  //   Line Number
  //   (Hexadecimal)
  //   End Screen Detector
  //   Remarque :
  //   200
  //   Front Porch Detector
  //   600
  //   Front Porch Detector
  //   and line number.
  //   210
  //   601
  //   The two seven segment displays are not part
  //   of the project, they are used for debugging
  //   puposes, mainely used to indicate the pixel
  //   Sync Pulse Detector
  //   Sync Pulse Detector
  //   242
  //   Back Porch Detector
  //   605
  //   Back Porch Detector
  //   264
  //   628
  //   Effective Pixel
  //   Signal
  //   Active Line
  //   Signal
  //   Remarque :
  //   The faulty red signal will fade off
  //   after one screen pass iteration.
  //   Sync Pulse
  //   Signal
  //   Sync Pulse
  //   Signal
  //   Remarque :
  //    this case.
  //   their usage is equivalent in
  //   The 27C512 EPROM is used
  //   instead of 28C256 EEPROM,
  //   Remarque :
  //   The resistors ladder
  //   is not implemented.
  //   Horizontal Sync Signal
  //   Vertical Sync Signal
endmodule
