// Logisim project SimpleVGACard.circ as structural Verilog: 3 circuits, main circuit main
module main (
);

  wire _200_out, _210_out, _242_out, _264_out, _600_out, _601_out, _605_out, _628_out, and_1_out,
       clock_1_out, nand_1_out, nand_2_out, nand_3_out, nand_4_out, nand_5_out, nand_6_out, nand_7_out,
       nand_8_out, not_1_out, not_2_out, not_3_out, not_4_out, not_5_out, not_6_out, not_7_out, not_8_out,
       not_9_out, not_10_out, not_11_out, not_12_out, not_13_out, not_14_out, not_15_out, not_16_out,
       not_17_out, not_18_out, not_19_out;
  wire [0:0] counter_10_bits_1_output_0, counter_10_bits_1_output_8;
  wire [2:0] counter_10_bits_2_output_0;
  wire [7:0] rom_1_data;
  wire [13:0] counter_10_bits_1_output_1;

  Clock clock_1 (.out(clock_1_out));
  Counter__10_bits counter_10_bits_1 (
    .Load(1'b0), .CLK(clock_1_out), .reset(_264_out), .Output_0(counter_10_bits_1_output_0[0]),
    .Output_1(counter_10_bits_1_output_1[0]), .Output_2(counter_10_bits_1_output_1[1]),
    .Output_3(counter_10_bits_1_output_1[2]), .Output_4(counter_10_bits_1_output_1[3]),
    .Output_5(counter_10_bits_1_output_1[4]), .Output_6(counter_10_bits_1_output_1[5]),
    .Output_7(counter_10_bits_1_output_1[6]), .Output_8(counter_10_bits_1_output_8[0]));  // open: Enable, Input_0, Input_1, Input_2, Input_3, Input_4, Input_5, Input_6, Input_7, Input_8, Output_9, Input_9, Cout
  Counter__10_bits counter_10_bits_2 (
    .Load(1'b0), .CLK(_264_out), .reset(_628_out), .Output_0(counter_10_bits_2_output_0[0]),
    .Output_1(counter_10_bits_2_output_0[1]), .Output_2(counter_10_bits_2_output_0[2]),
    .Output_3(counter_10_bits_1_output_1[7]), .Output_4(counter_10_bits_1_output_1[8]),
    .Output_5(counter_10_bits_1_output_1[9]), .Output_6(counter_10_bits_1_output_1[10]),
    .Output_7(counter_10_bits_1_output_1[11]), .Output_8(counter_10_bits_1_output_1[12]),
    .Output_9(counter_10_bits_1_output_1[13]));  // open: Enable, Input_0, Input_1, Input_2, Input_3, Input_4, Input_5, Input_6, Input_7, Input_8, Input_9, Cout
  not not_1 (not_1_out, counter_10_bits_1_output_0[0]);
  not not_2 (not_2_out, counter_10_bits_1_output_1[0]);
  not not_3 (not_3_out, counter_10_bits_1_output_1[1]);
  not not_4 (not_4_out, counter_10_bits_1_output_1[2]);
  not not_5 (not_5_out, counter_10_bits_1_output_1[3]);
  not not_6 (not_6_out, counter_10_bits_1_output_1[4]);
  not not_7 (not_7_out, counter_10_bits_1_output_1[5]);
  not not_8 (not_8_out, counter_10_bits_1_output_1[6]);
  not not_9 (not_9_out, counter_10_bits_1_output_8[0]);
  Hex_Digit_Display hex_digit_display_1 (.value({2'b00, counter_10_bits_1_output_1[13:12]}));  // open: dp
  not not_10 (not_10_out, counter_10_bits_2_output_0[0]);
  not not_11 (not_11_out, counter_10_bits_2_output_0[1]);
  not not_12 (not_12_out, counter_10_bits_2_output_0[2]);
  not not_13 (not_13_out, counter_10_bits_1_output_1[7]);
  not not_14 (not_14_out, counter_10_bits_1_output_1[8]);
  not not_15 (not_15_out, counter_10_bits_1_output_1[9]);
  not not_16 (not_16_out, counter_10_bits_1_output_1[10]);
  not not_17 (not_17_out, counter_10_bits_1_output_1[11]);
  not not_18 (not_18_out, counter_10_bits_1_output_1[12]);
  not not_19 (not_19_out, counter_10_bits_1_output_1[13]);
  Hex_Digit_Display hex_digit_display_2 (.value({3'b000, counter_10_bits_1_output_8[0]}));  // open: dp
  Hex_Digit_Display hex_digit_display_3 (.value(counter_10_bits_1_output_1[6:3]));  // open: dp
  Hex_Digit_Display hex_digit_display_4 (.value(counter_10_bits_1_output_1[11:8]));  // open: dp
  Hex_Digit_Display hex_digit_display_5 (.value({counter_10_bits_1_output_1[7], counter_10_bits_2_output_0}));  // open: dp
  Hex_Digit_Display hex_digit_display_6 (.value({counter_10_bits_1_output_1[2:0], counter_10_bits_1_output_0[0]}));  // open: dp
  nand _600 (_600_out, counter_10_bits_1_output_1[13], not_18_out, not_17_out, counter_10_bits_1_output_1[10], not_15_out, counter_10_bits_1_output_1[8], counter_10_bits_1_output_1[7], not_12_out, not_11_out, not_10_out);
  nand _200 (_200_out, not_9_out, counter_10_bits_1_output_1[6], counter_10_bits_1_output_1[5], not_6_out, not_5_out, counter_10_bits_1_output_1[2], not_3_out, not_2_out, not_1_out);
  nand _210 (_210_out, not_9_out, counter_10_bits_1_output_1[6], counter_10_bits_1_output_1[5], not_6_out, counter_10_bits_1_output_1[3], not_4_out, not_3_out, counter_10_bits_1_output_1[0], not_1_out);
  nand _601 (_601_out, counter_10_bits_1_output_1[13], not_18_out, not_17_out, counter_10_bits_1_output_1[10], not_15_out, counter_10_bits_1_output_1[8], counter_10_bits_1_output_1[7], not_12_out, not_11_out, counter_10_bits_2_output_0[0]);
  nand _242 (_242_out, not_9_out, counter_10_bits_1_output_1[6], counter_10_bits_1_output_1[5], counter_10_bits_1_output_1[4], counter_10_bits_1_output_1[3], not_4_out, not_3_out, counter_10_bits_1_output_1[0], not_1_out);
  nand _605 (_605_out, counter_10_bits_1_output_1[13], not_18_out, not_17_out, counter_10_bits_1_output_1[10], not_15_out, counter_10_bits_1_output_1[8], counter_10_bits_1_output_1[7], counter_10_bits_2_output_0[2], not_11_out, counter_10_bits_2_output_0[0]);
  nand _264 (_264_out, counter_10_bits_1_output_8[0], not_8_out, not_7_out, not_6_out, not_5_out, counter_10_bits_1_output_1[2], not_3_out, not_2_out, not_1_out);
  nand _628 (_628_out, counter_10_bits_1_output_1[13], not_18_out, not_17_out, counter_10_bits_1_output_1[10], counter_10_bits_1_output_1[9], counter_10_bits_1_output_1[8], not_13_out, counter_10_bits_2_output_0[2], not_11_out, not_10_out);
  nand nand_1 (nand_1_out, _210_out, nand_2_out);
  nand nand_2 (nand_2_out, nand_1_out, _242_out);
  nand nand_3 (nand_3_out, _264_out, nand_4_out);
  nand nand_4 (nand_4_out, nand_3_out, _200_out);
  nand nand_5 (nand_5_out, _601_out, nand_6_out);
  nand nand_6 (nand_6_out, nand_5_out, _605_out);
  nand nand_7 (nand_7_out, _628_out, nand_8_out);
  nand nand_8 (nand_8_out, nand_7_out, _600_out);
  and and_1 (and_1_out, nand_3_out, nand_7_out);
  ROM #(.addrWidth(15)) rom_1 (.addr({1'b0, counter_10_bits_1_output_1}), .data(rom_1_data), .sel(and_1_out));
  LED led_1 (.in(nand_1_out));
  LED led_2 (.in(nand_5_out));
  LED Blue_Signal (.in(rom_1_data[0]));
  LED Green_Signal (.in(rom_1_data[2]));
  LED Red_Signal (.in(rom_1_data[4]));

  // Notes on the sheet:
  //   10 MHz Clock
  //   Reset
  //   Reset
  //   Pixel Number
  //   (Hexadecimal)
  //   Line Number
  //   (Hexadecimal)
  //   End Screen Detector
  //   Front Porch Detector
  //   End Line Detector
  //   Front Porch Detector
  //   Remarque :
  //   and line number.
  //   Sync Pulse Detector
  //   Sync Pulse Detector
  //   The two seven segment displays are not part
  //   of the project, they are used for debugging
  //   puposes, mainely used to indicate the pixel
  //   Back Porch Detector
  //   Back Porch Detector
  //   Sync Pulse
  //   Generator
  //   Effective Pixel
  //   Detector
  //   Sync Pulse
  //   Generator
  //   Active Line
  //   Detector
  //   ROM
  //   Remarque :
  //   The faulty red signal will fade off
  //   after one screen pass iteration.
  //   Remarque :
  //   Horizontal Sync Signal
  //   The resistors ladder
  //   is not implemented.
  //   Vertical Sync Signal
endmodule

// Counter
module Counter__10_bits (
  input  Enable,
  input  Load,
  input  CLK,
  input  reset,
  input  Input_0,
  input  Input_1,
  input  Input_2,
  input  Input_3,
  input  Input_4,
  input  Input_5,
  input  Input_6,
  input  Input_7,
  input  Input_8,
  input  Input_9,
  output Output_0,
  output Output_1,
  output Output_2,
  output Output_3,
  output Output_4,
  output Output_5,
  output Output_6,
  output Output_7,
  output Output_8,
  output Output_9,
  output Cout
);

  wire and_1_out, and_2_out, and_3_out, and_4_out, and_5_out, and_6_out, and_7_out, and_8_out, and_9_out,
       mux_2_1_1_bit_1_output, mux_2_1_1_bit_2_output, mux_2_1_1_bit_3_output, mux_2_1_1_bit_4_output,
       mux_2_1_1_bit_5_output, mux_2_1_1_bit_6_output, mux_2_1_1_bit_7_output, mux_2_1_1_bit_8_output,
       mux_2_1_1_bit_9_output, mux_2_1_1_bit_10_output, not_1_out, xor_1_out, xor_2_out, xor_3_out,
       xor_4_out, xor_5_out, xor_6_out, xor_7_out, xor_8_out, xor_9_out, xor_10_out;

  Mux_2_1__1_bit mux_2_1_1_bit_1 (.Input_0(Enable), .Input_1(Input_0), .Output(mux_2_1_1_bit_1_output), .Select(Load));
  Mux_2_1__1_bit mux_2_1_1_bit_2 (
    .Input_0(and_1_out), .Input_1(Input_1), .Output(mux_2_1_1_bit_2_output), .Select(Load));
  Mux_2_1__1_bit mux_2_1_1_bit_3 (
    .Input_0(and_2_out), .Input_1(Input_2), .Output(mux_2_1_1_bit_3_output), .Select(Load));
  Mux_2_1__1_bit mux_2_1_1_bit_4 (
    .Input_0(and_3_out), .Input_1(Input_3), .Output(mux_2_1_1_bit_4_output), .Select(Load));
  Mux_2_1__1_bit mux_2_1_1_bit_5 (
    .Input_0(and_4_out), .Input_1(Input_4), .Output(mux_2_1_1_bit_5_output), .Select(Load));
  Mux_2_1__1_bit mux_2_1_1_bit_6 (
    .Input_0(and_5_out), .Input_1(Input_5), .Output(mux_2_1_1_bit_6_output), .Select(Load));
  Mux_2_1__1_bit mux_2_1_1_bit_7 (
    .Input_0(and_6_out), .Input_1(Input_6), .Output(mux_2_1_1_bit_7_output), .Select(Load));
  Mux_2_1__1_bit mux_2_1_1_bit_8 (
    .Input_0(and_7_out), .Input_1(Input_7), .Output(mux_2_1_1_bit_8_output), .Select(Load));
  Mux_2_1__1_bit mux_2_1_1_bit_9 (
    .Input_0(and_8_out), .Input_1(Input_8), .Output(mux_2_1_1_bit_9_output), .Select(Load));
  Mux_2_1__1_bit mux_2_1_1_bit_10 (
    .Input_0(and_9_out), .Input_1(Input_9), .Output(mux_2_1_1_bit_10_output), .Select(Load));
  xor xor_1 (xor_1_out, Load, mux_2_1_1_bit_1_output);
  xor xor_2 (xor_2_out, Load, mux_2_1_1_bit_2_output);
  xor xor_3 (xor_3_out, Load, mux_2_1_1_bit_3_output);
  xor xor_4 (xor_4_out, Load, mux_2_1_1_bit_4_output);
  xor xor_5 (xor_5_out, Load, mux_2_1_1_bit_5_output);
  xor xor_6 (xor_6_out, Load, mux_2_1_1_bit_6_output);
  xor xor_7 (xor_7_out, Load, mux_2_1_1_bit_7_output);
  xor xor_8 (xor_8_out, Load, mux_2_1_1_bit_8_output);
  xor xor_9 (xor_9_out, Load, mux_2_1_1_bit_9_output);
  xor xor_10 (xor_10_out, Load, mux_2_1_1_bit_10_output);
  not not_1 (not_1_out, reset);
  J_K_Flip_Flop j_k_ff_1 (
    .J(mux_2_1_1_bit_1_output), .clk(CLK), .K(xor_1_out), .Q(Output_0), .reset(not_1_out));  // open: Qn, preset, en
  and and_1 (and_1_out, Output_0, Enable);
  J_K_Flip_Flop j_k_ff_2 (
    .J(mux_2_1_1_bit_2_output), .clk(CLK), .K(xor_2_out), .Q(Output_1), .reset(not_1_out));  // open: Qn, preset, en
  and and_2 (and_2_out, Output_1, and_1_out);
  J_K_Flip_Flop j_k_ff_3 (
    .J(mux_2_1_1_bit_3_output), .clk(CLK), .K(xor_3_out), .Q(Output_2), .reset(not_1_out));  // open: Qn, preset, en
  and and_3 (and_3_out, Output_2, and_2_out);
  J_K_Flip_Flop j_k_ff_4 (
    .J(mux_2_1_1_bit_4_output), .clk(CLK), .K(xor_4_out), .Q(Output_3), .reset(not_1_out));  // open: Qn, preset, en
  and and_4 (and_4_out, Output_3, and_3_out);
  J_K_Flip_Flop j_k_ff_5 (
    .J(mux_2_1_1_bit_5_output), .clk(CLK), .K(xor_5_out), .Q(Output_4), .reset(not_1_out));  // open: Qn, preset, en
  and and_5 (and_5_out, Output_4, and_4_out);
  J_K_Flip_Flop j_k_ff_6 (
    .J(mux_2_1_1_bit_6_output), .clk(CLK), .K(xor_6_out), .Q(Output_5), .reset(not_1_out));  // open: Qn, preset, en
  and and_6 (and_6_out, Output_5, and_5_out);
  J_K_Flip_Flop j_k_ff_7 (
    .J(mux_2_1_1_bit_7_output), .clk(CLK), .K(xor_7_out), .Q(Output_6), .reset(not_1_out));  // open: Qn, preset, en
  and and_7 (and_7_out, Output_6, and_6_out);
  J_K_Flip_Flop j_k_ff_8 (
    .J(mux_2_1_1_bit_8_output), .clk(CLK), .K(xor_8_out), .Q(Output_7), .reset(not_1_out));  // open: Qn, preset, en
  and and_8 (and_8_out, Output_7, and_7_out);
  J_K_Flip_Flop j_k_ff_9 (
    .J(mux_2_1_1_bit_9_output), .clk(CLK), .K(xor_9_out), .Q(Output_8), .reset(not_1_out));  // open: Qn, preset, en
  and and_9 (and_9_out, Output_8, and_8_out);
  J_K_Flip_Flop j_k_ff_10 (
    .J(mux_2_1_1_bit_10_output), .clk(CLK), .K(xor_10_out), .Q(Output_9), .reset(not_1_out));  // open: Qn, preset, en
  and and_10 (Cout, Output_9, and_9_out);

  // Notes on the sheet:
  //   Enable: pull=up
  //   Load: pull=down
endmodule

module Mux_2_1__1_bit (
  input  Select,
  input  Input_0,
  input  Input_1,
  output Output
);

  wire and_1_out, and_2_out, not_1_out;

  not not_1 (not_1_out, Select);
  and and_1 (and_1_out, not_1_out, Input_0);
  and and_2 (and_2_out, Select, Input_1);
  or or_1 (Output, and_1_out, and_2_out);
endmodule
